# Fritzing sketch Spectrum Visualizer circuit (saved by Fritzing 0.9.3b)
breadboards: 1

parts:
  Bauteil1 = Arduino Uno (Rev3)
  Bauteil2 = NeoPixel Stick [part_number=1426]
  S1 = Momentary Switch [package=ksa_sealed_tac_switch]
  S2 = Momentary Switch [package=ksa_sealed_tac_switch]
  S3 = Momentary Switch [package=ksa_sealed_tac_switch]
  Squix1 = OLED 0.96" 128x64 I2C SSD1306

nets:
  N1: Bauteil1.D11_PWM/MOSI, S2.4
  N2: Bauteil1.D12/MISO, S1.4
  N3: Bauteil1.D13/SCK, Bauteil2.DATAIN
  N4: Bauteil1.A4/SDA, Squix1.SCA
  N5: Bauteil1.A5/SCL, Squix1.SCL
  N6: Bauteil1.D3_PWM, S3.4
  5V: Bauteil1.5V, Bauteil2.+5V, Squix1.VCC
  GND: Bauteil1.GND, Bauteil2.GND, S1.1, S2.1, S3.1, Squix1.GND

notes:
  Up Button
  Down Button
  Select Button
  Just imagine the spectrum shield on top of the Arduino. Fritzing does not have that board to show
  Connect your LED Strip like this
  5V to 5V
  Pin 13 to Data In
  GND to GND

custom parts:
  NeoPixel Stick: Make your own little LED strip arrangement with this stick of NeoPixel LEDs. We crammed 8 of the tiny 5050 (5mm x 5mm) smart RGB LEDs onto a PCB with mounting holes and a chainable design. Use only one microcontroller pin to control as many as you can chain together! Each LED is addressable as the driver chip is inside the LED. Each one has ~18mA constant current drive so the color will be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
